# Fritzing sketch ESP32_ServoMotor_LED (saved by Fritzing 0.9.6b)
breadboards: 1

parts:
  Mod1 = Heltec WiFi LoRa 32 V2 [part_number=HTIT-WB32LA]
  M1 = Dagu DGServo 9g (End View) [part_number=RS001B]
  LED1 = LED - 5mm [color="Red (633nm)" current=0.030 package="5 mm [THT]"]
  R1 = Resistor [tolerance=±5% power=0.25 resistance=220 package=THT]
  VCC1 = Battery

nets:
  N1: Mod1.pin_9, R1.Pin_1
  N2: Mod1.pin_16, Mod1.pin_17
  GND: Mod1.GND, M1.gnd, LED1.cathode, VCC1.-
  N3: Mod1.pin_21, Mod1.pin_22
  N4: Mod1.pin_36, M1.pulse
  N5: M1.vcc, VCC1.+
  N6: LED1.anode, R1.Pin_0
